// Logisim project CPU.circ as structural Verilog: 8 circuits, main circuit CPU
module CPU (
);

  wire K0, K1, K2, K3, L0, L1, L2, L3, L4, L5, L6, L7, L8, L9, or_1_out, or_2_out, S0, S1, S2, S3, S4, S5,
       S6, S7, S8, S9, uc_1_clr_count, uc_1_clr_rg, uc_1_jmp, uc_1_load_rg1, uc_1_load_rg2;
  wire [1:0] uc_1_ula;
  wire [3:0] HEX0, HEX1, HEX2, HEX3, HEX4, HEX5, uc_1_operando, uc_1_rgin, ula4_1_rgto;

  LED u_L9 (.in(L9));
  // DipSwitch #(.NSwitches(1)) S9: pin names not known; wires that end beside it: S9
  Hex_Digit_Display hex_digit_display_1 (.value(HEX5));  // open: dp
  Hex_Digit_Display hex_digit_display_2 (.value(HEX4));  // open: dp
  LED u_L8 (.in(L8));
  LED u_L7 (.in(L7));
  // DipSwitch #(.NSwitches(1)) S6: pin names not known; wires that end beside it: S6
  // DipSwitch #(.NSwitches(1)) S8: pin names not known; wires that end beside it: S8
  // DipSwitch #(.NSwitches(1)) S7: pin names not known; wires that end beside it: S7
  or or_1 (or_1_out, S0, uc_1_clr_count);
  Hex_Digit_Display hex_digit_display_3 (.value(HEX2));  // open: dp
  Hex_Digit_Display hex_digit_display_4 (.value(HEX3));  // open: dp
  LED u_L5 (.in(L5));
  LED u_L4 (.in(L4));
  LED u_L6 (.in(L6));
  // DipSwitch #(.NSwitches(1)) S4: pin names not known; wires that end beside it: S4
  // DipSwitch #(.NSwitches(1)) S5: pin names not known; wires that end beside it: S5
  Count8 count8_1 (
    .CLR(or_1_out), .JMP(uc_1_jmp), .CLK(S9), .Addr(uc_1_operando), .Cont({L7, L6, L5, L4, L3, L2, L1, L0}));
  Hex_Digit_Display hex_digit_display_5 (.value(HEX1));  // open: dp
  LED u_L1 (.in(L1));
  LED u_L3 (.in(L3));
  LED u_L2 (.in(L2));
  // DipSwitch #(.NSwitches(1)) S2: pin names not known; wires that end beside it: S2
  // DipSwitch #(.NSwitches(1)) S3: pin names not known; wires that end beside it: S3
  // DipSwitch #(.NSwitches(1)) S1: pin names not known; wires that end beside it: {HEX5, HEX4, HEX3, HEX2}, S1
  ROM_256x16_2 rom_256x16_2_1 (.Addr({L7, L6, L5, L4, L3, L2, L1, L0}), .Data({HEX5, HEX4, HEX3, HEX2}), .CLK(S9));
  or or_2 (or_2_out, S0, uc_1_clr_rg);
  Hex_Digit_Display hex_digit_display_6 (.value(HEX0));  // open: dp
  LED u_L0 (.in(L0));
  // DipSwitch #(.NSwitches(1)) S0: pin names not known; wires that end beside it: S0
  Button u_K3 (.out(K3));
  Reg4 reg4_1 (.CLK(S9), .Load(uc_1_load_rg1), .Q(HEX1), .D(ula4_1_rgto), .CLR(or_2_out));
  Button u_K2 (.out(K2));
  Button u_K1 (.out(K1));
  Button u_K0 (.out(K0));
  UC uc_1 (
    .Data({HEX5, HEX4, HEX3, HEX2}), .Rg1(HEX1), .Rg2(HEX0), .Operando(uc_1_operando), .CLR_Rg(uc_1_clr_rg),
    .ULA(uc_1_ula), .CLR_Count(uc_1_clr_count), .JMP(uc_1_jmp), .RgIN(uc_1_rgin), .Load_Rg1(uc_1_load_rg1),
    .Load_Rg2(uc_1_load_rg2));  // open: Disponivel
  ULA4 ula4_1 (.RgIN(uc_1_rgin), .Operando(uc_1_operando), .RgTO(ula4_1_rgto), .Sel(uc_1_ula));
  Reg4 reg4_2 (.CLK(S9), .Load(uc_1_load_rg2), .Q(HEX0), .D(ula4_1_rgto), .CLR(or_2_out));

  // Other names for the same wires on the sheet: Hexs_Data[15:0] = {HEX5, HEX4, HEX3, HEX2};
  //   LEDs_Count[7:0] = {L7, L6, L5, L4, L3, L2, L1, L0}
endmodule

module UC (
  input  [15:0] Data,
  input  [3:0] Rg1,
  input  [3:0] Rg2,
  output [3:0] Operando,
  output [3:0] Disponivel,
  output CLR_Rg,
  output [1:0] ULA,
  output CLR_Count,
  output JMP,
  output [3:0] RgIN,
  output Load_Rg1,
  output Load_Rg2
);

  wire decoder_1_out0, decoder_1_out1, not_1_out;

  Multiplexer #(.width(4), .enable("false")) multiplexer_1 (.in0(Rg2), .in1(Rg1), .out(RgIN), .sel(Data[12]));
  Decoder #(.select(2), .enable("false")) decoder_1 (
    .out0(decoder_1_out0), .out1(decoder_1_out1), .out2(CLR_Count), .out3(JMP), .sel(Data[11:10]));
  and and_1 (Load_Rg1, Data[14], decoder_1_out0);
  not not_1 (not_1_out, Data[14]);
  and and_2 (Load_Rg2, not_1_out, decoder_1_out0);
  or or_1 (CLR_Rg, decoder_1_out1, CLR_Count);

  assign Disponivel = Data[7:4];
  assign Operando = Data[3:0];
  assign ULA = Data[9:8];
endmodule

module ULA4 (
  input  [3:0] Operando,
  input  [3:0] RgIN,
  input  [1:0] Sel,
  output [3:0] RgTO
);

  wire [3:0] adder_1_out, divider_1_out, multiplier_1_out, subtractor_1_out;

  Adder #(.width(4)) adder_1 (.a(Operando), .b(RgIN), .out(adder_1_out));  // open: cin, cout
  Multiplier #(.width(4)) multiplier_1 (.a(Operando), .b(4'b0010), .out(multiplier_1_out));  // open: cin, cout
  Subtractor #(.width(4)) subtractor_1 (.a(RgIN), .b(Operando), .out(subtractor_1_out));  // open: bin, bout
  Divider #(.width(4)) divider_1 (.a(Operando), .b(4'b0010), .out(divider_1_out));  // open: upper, rem
  Multiplexer #(.select(2), .width(4), .enable("false")) multiplexer_1 (
    .in0(adder_1_out), .in1(multiplier_1_out), .in2(subtractor_1_out), .in3(divider_1_out), .out(RgTO),
    .sel(Sel));
endmodule

module Reg4 (
  input  CLK,
  input  Load,
  input  [3:0] D,
  input  CLR,
  output [3:0] Q
);

  wire and_1_out, multiplexer_1_out, multiplexer_2_out, multiplexer_3_out, multiplexer_4_out, not_1_out;

  not not_1 (not_1_out, CLK);
  Multiplexer #(.enable("false")) multiplexer_1 (.in0(Q[3]), .in1(D[3]), .out(multiplexer_1_out), .sel(Load));
  and and_1 (and_1_out, not_1_out, CLR);
  D_Flip_Flop d_ff_1 (.clk(not_1_out), .D(multiplexer_1_out), .Q(Q[3]), .reset(and_1_out));  // open: Qn, preset
  Multiplexer #(.enable("false")) multiplexer_2 (.in0(Q[2]), .in1(D[2]), .out(multiplexer_2_out), .sel(Load));
  D_Flip_Flop d_ff_2 (.clk(not_1_out), .D(multiplexer_2_out), .Q(Q[2]), .reset(and_1_out));  // open: Qn, preset
  Multiplexer #(.enable("false")) multiplexer_3 (.in0(Q[1]), .in1(D[1]), .out(multiplexer_3_out), .sel(Load));
  D_Flip_Flop d_ff_3 (.clk(not_1_out), .D(multiplexer_3_out), .Q(Q[1]), .reset(and_1_out));  // open: Qn, preset
  Multiplexer #(.enable("false")) multiplexer_4 (.in0(Q[0]), .in1(D[0]), .out(multiplexer_4_out), .sel(Load));
  D_Flip_Flop d_ff_4 (.clk(not_1_out), .D(multiplexer_4_out), .Q(Q[0]), .reset(and_1_out));  // open: Qn, preset
endmodule

module Count8 (
  input  [3:0] Addr,
  input  JMP,
  input  CLK,
  input  CLR,
  output [7:0] Cont
);

  wire and_1_out, and_2_out, and_3_out, and_4_out, and_5_out, and_6_out, and_7_out, not_1_out, not_2_out;

  not not_1 (not_1_out, CLK);
  not not_2 (not_2_out, CLR);
  and and_1 (and_1_out, JMP, not_1_out);
  Flip_Flop_T_JMP ff_t_jmp_1 (.Addr(Addr[0]), .JMP(and_1_out), .CLK(not_1_out), .T(1'b1), .CLR(not_2_out), .Q(Cont[0]));
  Flip_Flop_T_JMP ff_t_jmp_2 (
    .Addr(Addr[1]), .JMP(and_1_out), .CLK(not_1_out), .T(Cont[0]), .CLR(not_2_out), .Q(Cont[1]));
  and and_2 (and_2_out, Cont[1], Cont[0]);
  Flip_Flop_T_JMP ff_t_jmp_3 (
    .Addr(Addr[2]), .JMP(and_1_out), .CLK(not_1_out), .T(and_2_out), .CLR(not_2_out), .Q(Cont[2]));
  and and_3 (and_3_out, Cont[2], and_2_out);
  Flip_Flop_T_JMP ff_t_jmp_4 (
    .Addr(Addr[3]), .JMP(and_1_out), .CLK(not_1_out), .T(and_3_out), .CLR(not_2_out), .Q(Cont[3]));
  and and_4 (and_4_out, Cont[3], and_3_out);
  Flip_Flop_T_JMP ff_t_jmp_5 (
    .Addr(1'b0), .JMP(and_1_out), .CLK(not_1_out), .T(and_4_out), .CLR(not_2_out), .Q(Cont[4]));
  and and_5 (and_5_out, Cont[4], and_4_out);
  Flip_Flop_T_JMP ff_t_jmp_6 (
    .Addr(1'b0), .JMP(and_1_out), .CLK(not_1_out), .T(and_5_out), .CLR(not_2_out), .Q(Cont[5]));
  and and_6 (and_6_out, Cont[5], and_5_out);
  Flip_Flop_T_JMP ff_t_jmp_7 (.Addr(1'b0), .JMP(and_1_out), .CLK(not_1_out), .CLR(not_2_out), .Q(Cont[6]));  // open: T
  and and_7 (and_7_out, Cont[6], and_6_out);
  Flip_Flop_T_JMP ff_t_jmp_8 (
    .Addr(1'b0), .JMP(and_1_out), .CLK(not_1_out), .T(and_7_out), .CLR(not_2_out), .Q(Cont[7]));
endmodule

module Flip_Flop_T_JMP (
  input  Addr,
  input  JMP,
  input  CLK,
  input  T,
  input  CLR,
  output Q
);

  wire and_1_out, nand_1_out, not_1_out, or_1_out;

  not not_1 (not_1_out, JMP);
  nand nand_1 (nand_1_out, Addr, JMP);
  or or_1 (or_1_out, Addr, not_1_out);
  and and_1 (and_1_out, or_1_out, CLR);
  T_Flip_Flop #(.NegatePresetClear("true")) t_ff_1 (
    .clk(CLK), .T(T), .Q(Q), .preset(nand_1_out), .reset(and_1_out));  // open: Qn
endmodule

module ROM_256x16_1 (
  input  [7:0] Addr,
  input  CLK,
  output [15:0] Data
);

  wire [15:0] ROM_256x16_data;

  Register #(.width(16), .Select("low")) Reg16 (.D(ROM_256x16_data), .Q(Data), .clk(CLK));  // open: en, clr
  ROM #(.dataWidth(16), .Select("low")) ROM_256x16 (.addr(Addr), .data(ROM_256x16_data));

  // Notes on the sheet:
  //   contents of ROM_256x16 (hex, n*v repeats v):
  //   6005 9101 6202 6304 c08 0 0 0 400 6001 9001 9002 6302 6102 9302 6200 6001 800
endmodule

module ROM_256x16_2 (
  input  [7:0] Addr,
  input  CLK,
  output [15:0] Data
);

  wire [15:0] ROM_256x16_data;

  Register #(.width(16), .Select("low")) Reg16 (.D(ROM_256x16_data), .Q(Data), .clk(CLK));  // open: en, clr
  ROM #(.dataWidth(16), .Select("low")) ROM_256x16 (.addr(Addr), .data(ROM_256x16_data));

  // Notes on the sheet:
  //   contents of ROM_256x16 (hex, n*v repeats v):
  //   6004 9102 6201 6305 9002 6002 9003 400 c0d 4*0 9002 6302 6101 9302 6200 6003 800
endmodule
